# Fritzing sketch RaspBerryPI3_FT (saved by Fritzing 0.9.3b)
breadboards: 1

parts:
  Raspberry_Pi_1 = Raspberry Pi 3 [part_number=RPI-3-V1.2]
  LED1 = LED - 5mm [color="Red (633nm)" package="5 mm [THT]"]
  LED2 = LED - 3mm [color="Green (555nm)" package="3 mm [THT]"]
  S1 = SWITCH-MOMENTARY-2 [package=tactile-pth-12mm]
  S2 = SWITCH-MOMENTARY-2 [package=tactile-pth-12mm]
  S3 = SWITCH-MOMENTARY-2 [package=tactile-pth-12mm]
  S4 = SWITCH-MOMENTARY-2 [package=tactile-pth-12mm]
  R1 = Resistor [tolerance=±5% resistance=220 package="0402 [SMD]"]
  R2 = Resistor [tolerance=±5% resistance=220 package="2010 [SMD]"]
  R3 = Resistor [tolerance=±5% resistance=220 package=THT]
  R4 = Resistor [tolerance=±5% resistance=220 package=THT]
  R5 = Resistor [tolerance=±5% resistance=220 package=THT]
  R6 = Resistor [tolerance=±5% resistance=220 package=THT]

nets:
  N1: Raspberry_Pi_1.GPIO4, S4.2
  N2: Raspberry_Pi_1.GPIO26, R6.Pin_0
  N3: Raspberry_Pi_1.GPIO20, R5.Pin_0
  N4: Raspberry_Pi_1.GPIO23, S1.2
  N5: Raspberry_Pi_1.GPIO18, S2.2
  N6: Raspberry_Pi_1.GPIO15, S3.2
  N7: Raspberry_Pi_1.GND, LED1.cathode, LED2.cathode, R1.Pin_1, R2.Pin_1, R3.Pin_1, R4.Pin_1
  N8: LED1.anode, R6.Pin_1
  N9: LED2.anode, R5.Pin_1
  N10: S1.1, R1.Pin_0
  N11: S2.1, R2.Pin_0
  N12: S3.1, R3.Pin_0
  N13: S4.1, R4.Pin_0

// code stored in the sketch: codigo_RBFT.ino
const int ledPinVermelho = 26;	//ledPinVermelho == pino 9
const int ledPinVerde = 20;	//ledPinVerde == pino 8

const int pinoDois = 4; 	//pinoDois == pino 2
const int pinoTres = 15; 	//pinoTres == pino 3
const int pinoQuatro = 18;	//pinoQuatro == pino 4
const int pinoCinco = 23;	//pinoCinco == pino 5

int estadoPinoDois = 0;		// verificadores dos
int estadoPinoTres = 0;		// estados dos botões
int estadoPinoQuatro = 0;	// respectivos(verifica se
int estadoPinoCinco = 0;	// está HIGH ou LOW)

void setup()
{
  pinMode(ledPinVermelho, OUTPUT);
  pinMode(ledPinVerde, OUTPUT);
  
  pinMode(pinoDois, INPUT);
  pinMode(pinoTres, INPUT);
  pinMode(pinoQuatro, INPUT);
  pinMode(pinoCinco, INPUT);
}

void loop()
{
  estadoPinoDois = digitalRead(pinoDois);
  estadoPinoTres = digitalRead(pinoTres);
  estadoPinoQuatro = digitalRead(pinoQuatro);
  estadoPinoCinco = digitalRead(pinoCinco);
  
  if(estadoPinoDois == HIGH || estadoPinoQuatro == HIGH){
  	digitalWrite(ledPinVerde, HIGH);
  }else digitalWrite(ledPinVerde, LOW);
  
  if(estadoPinoTres == HIGH || estadoPinoCinco == HIGH){
  	digitalWrite(ledPinVermelho, HIGH);
  }else digitalWrite(ledPinVermelho, LOW);
}
